// Logisim project Enigma.circ as structural Verilog: 10 circuits, main circuit main
module main (
  input  in_1,
  input  in_2
);

  wire CLOCK, counter_1_carry, counter_2_carry, deslocar;
  wire [4:0] bitselector_1_out, controller_1_out_3, controller_2_out_3, controller_3_out_3,
       controller_4_out_3, controller_inverso_1_out_3, controller_inverso_2_out_3,
       controller_inverso_3_out_3, counter_1_q, counter_2_q, counter_3_q, counter_4_q, Criptografar,
       Decriptografar, plugboard_1_out_2, plugboard_2_out_2, plugboard_3_out_2, plugboard_4_out_2,
       refletor_1_out_2, refletor_2_out_2, rotor1_1_out_2, rotor1_2_out_2, rotor1_inverso_1_out_2,
       rotor2_1_out_2, rotor2_2_out_2, rotor2_inverso_1_out_2, rotor2_inverso_2_out_2, rotor2_inverso_3_out_2;
  wire [6:0] bit_extender_1_out, bit_extender_2_out, demultiplexer_1_out1, multiplexer_1_out, sCodificada,
       sDecodificada, sNormal, Teclado;

  Clock clock_1 (.out(CLOCK));
  Keyboard #(.buflen(256)) keyboard_1 (.clk(CLOCK), .re(1'b1), .clr(in_1), .data(Teclado));  // open: avail
  Plugboard plugboard_1 (.\Seletor_endereço (Criptografar), .out_2(plugboard_1_out_2));
  Plugboard plugboard_2 (.\Seletor_endereço (Decriptografar), .out_2(plugboard_2_out_2));
  Rotor2 rotor2_1 (.\Seletor_endereço (controller_1_out_3), .out_2(rotor2_1_out_2));
  Controller controller_1 (.Letra(plugboard_1_out_2), .Deslocamento(counter_1_q), .out_3(controller_1_out_3));
  Controller__Inverso controller_inverso_1 (
    .Letra(rotor2_inverso_1_out_2), .Deslocamento(counter_2_q), .out_3(controller_inverso_1_out_3));
  Rotor2__Inverso rotor2_inverso_1 (.\Seletor_endereço (plugboard_2_out_2), .out_2(rotor2_inverso_1_out_2));
  Rotor1 rotor1_1 (.\Seletor_endereço (controller_2_out_3), .out_2(rotor1_1_out_2));
  Controller controller_2 (.Letra(rotor2_1_out_2), .Deslocamento(counter_3_q), .out_3(controller_2_out_3));
  Counter #(.width(5), .max('h1a)) counter_1 (
    .Q(counter_1_q), .carry(counter_1_carry), .clk(deslocar), .clr(in_1));  // open: load, D, count
  Refletor refletor_1 (.\Seletor_endereço (rotor2_inverso_2_out_2), .out_2(refletor_1_out_2));
  Rotor2__Inverso rotor2_inverso_2 (.\Seletor_endereço (controller_inverso_1_out_3), .out_2(rotor2_inverso_2_out_2));
  Counter #(.width(5), .max('h1a)) counter_2 (
    .Q(counter_2_q), .carry(counter_2_carry), .clk(deslocar), .clr(in_1));  // open: load, D, count
  Multiplexer #(.width(7), .enable("false")) multiplexer_1 (
    .in0(sCodificada), .in1(sDecodificada), .out(multiplexer_1_out), .sel(in_2));
  TTY #(.cols(16)) tty_1 (.data(multiplexer_1_out), .clk(CLOCK), .we(1'b1), .clr(in_1));
  Refletor refletor_2 (.\Seletor_endereço (rotor1_1_out_2), .out_2(refletor_2_out_2));
  Counter #(.width(5), .max('h1a)) counter_3 (
    .Q(counter_3_q), .clk(counter_1_carry), .clr(in_1));  // open: load, D, count, carry
  Controller__Inverso controller_inverso_2 (
    .Letra(refletor_1_out_2), .Deslocamento(counter_4_q), .out_3(controller_inverso_2_out_3));
  Counter #(.width(5), .max('h1a)) counter_4 (
    .Q(counter_4_q), .clk(counter_2_carry), .clr(in_1));  // open: load, D, count, carry
  Controller controller_3 (.Letra(refletor_2_out_2), .Deslocamento(counter_3_q), .out_3(controller_3_out_3));
  Rotor1__Inverso rotor1_inverso_1 (.\Seletor_endereço (controller_inverso_2_out_3), .out_2(rotor1_inverso_1_out_2));
  Rotor2__Inverso rotor2_inverso_3 (.\Seletor_endereço (rotor1_inverso_1_out_2), .out_2(rotor2_inverso_3_out_2));
  Rotor1 rotor1_2 (.\Seletor_endereço (controller_3_out_3), .out_2(rotor1_2_out_2));
  Controller controller_4 (.Letra(rotor1_2_out_2), .Deslocamento(counter_1_q), .out_3(controller_4_out_3));
  Controller__Inverso controller_inverso_3 (
    .Letra(rotor2_inverso_3_out_2), .Deslocamento(counter_2_q), .out_3(controller_inverso_3_out_3));
  Demultiplexer #(.width(7), .enable("false")) demultiplexer_1 (
    .out0(sNormal), .out1(demultiplexer_1_out1), .in(Teclado), .sel(deslocar));
  Verificador verificador_1 (.Verificar(Teclado), .out_2(deslocar));
  Rotor2 rotor2_2 (.\Seletor_endereço (controller_4_out_3), .out_2(rotor2_2_out_2));
  Plugboard plugboard_3 (.\Seletor_endereço (controller_inverso_3_out_3), .out_2(plugboard_3_out_2));
  BitSelector #(.width(7), .group(5)) bitselector_1 (.in(demultiplexer_1_out1), .out(bitselector_1_out), .sel(1'b0));
  Demultiplexer #(.width(5), .enable("false")) demultiplexer_2 (
    .out0(Criptografar), .out1(Decriptografar), .in(bitselector_1_out), .sel(in_2));
  Plugboard plugboard_4 (.\Seletor_endereço (rotor2_2_out_2), .out_2(plugboard_4_out_2));
  assign bit_extender_1_out = {{2{1'b1}}, plugboard_4_out_2};  // Bit_Extender bit_extender_1
  Multiplexer #(.width(7), .enable("false")) multiplexer_2 (
    .in0(sNormal), .in1(bit_extender_2_out), .out(sDecodificada), .sel(deslocar));
  assign bit_extender_2_out = {{2{1'b1}}, plugboard_3_out_2};  // Bit_Extender bit_extender_2
  Multiplexer #(.width(7), .enable("false")) multiplexer_3 (
    .in0(sNormal), .in1(bit_extender_1_out), .out(sCodificada), .sel(deslocar));

  // Other names for the same wires on the sheet: CLEAR = in_1; DECODIFICAR = in_2

  // Notes on the sheet:
  //   Plugboard
  //   Plugboard
  //   Rotor 2
  //   Rotor 2
  //   Rotor 1
  //   Refletor
  //   Refletor
  //   Rotor 1
  //   Rotor 1
  //   Rotor 2
  //   Rotor 2
  //   Plugboard
  //   Plugboard
endmodule

module Verificador (
  input  [6:0] Verificar,
  output out_2
);

  wire comparator_1_gt, comparator_2_lt;

  Comparator #(.width(7)) comparator_1 (.a(Verificar), .b(7'b1100000), .gt(comparator_1_gt));  // open: eq, lt
  and and_1 (out_2, comparator_1_gt, comparator_2_lt);
  Comparator #(.width(7)) comparator_2 (.a(Verificar), .b(7'b1111011), .lt(comparator_2_lt));  // open: gt, eq
endmodule

module Plugboard (
  input  [4:0] \Seletor_endereço ,
  output [4:0] out_2
);

  wire [6:0] rom_1_data;

  BitSelector #(.width(7), .group(5)) bitselector_1 (.in(rom_1_data), .out(out_2), .sel(1'b0));
  ROM #(.addrWidth(5), .dataWidth(7)) rom_1 (.addr(\Seletor_endereço ), .data(rom_1_data), .sel(1'b1));

  // Notes on the sheet:
  //   contents of rom_1 (hex, n*v repeats v):
  //   0 66 74 6d 67 7a 61 64 70 6f 6b 6a 77 63 73 69 68 78 79 6e 62 76 75 6c 71 72 65
endmodule

module Refletor (
  input  [4:0] \Seletor_endereço ,
  output [4:0] out_2
);

  wire [6:0] rom_1_data;

  BitSelector #(.width(7), .group(5)) bitselector_1 (.in(rom_1_data), .out(out_2), .sel(1'b0));
  ROM #(.addrWidth(5), .dataWidth(7)) rom_1 (.addr(\Seletor_endereço ), .data(rom_1_data), .sel(1'b1));

  // Notes on the sheet:
  //   contents of rom_1 (hex, n*v repeats v):
  //   0 74 68 69 67 66 65 64 62 63 77 73 71 78 76 7a 79 6c 75 6b 61 72 6e 6a 6d 70 6f
endmodule

module Controller (
  input  [4:0] Letra,
  input  [4:0] Deslocamento,
  output [4:0] out_3
);

  wire comparator_1_eq, Sub;
  wire [4:0] adder_1_out, multiplexer_1_out, subtractor_1_out;

  Adder #(.width(5)) adder_1 (.a(Letra), .b(Deslocamento), .out(adder_1_out));  // open: cin, cout
  Comparator #(.width(5), .mode("unsigned")) comparator_1 (
    .a(adder_1_out), .b({5{1'b0}}), .eq(comparator_1_eq));  // open: gt, lt
  Comparator #(.width(5), .mode("unsigned")) comparator_2 (.a(5'b11010), .b(adder_1_out), .lt(Sub));  // open: gt, eq
  Multiplexer #(.width(5), .enable("false")) multiplexer_1 (
    .in0(adder_1_out), .in1(5'b00001), .out(multiplexer_1_out), .sel(comparator_1_eq));
  Subtractor #(.width(5)) subtractor_1 (.a(adder_1_out), .b(5'b11010), .out(subtractor_1_out));  // open: bin, bout
  Multiplexer #(.width(5), .enable("false")) multiplexer_2 (
    .in0(multiplexer_1_out), .in1(subtractor_1_out), .out(out_3), .sel(Sub));
endmodule

// R1
module Rotor1 (
  input  [4:0] \Seletor_endereço ,
  output [4:0] out_2
);

  wire [6:0] rom_1_data;

  ROM #(.addrWidth(5), .dataWidth(7)) rom_1 (.addr(\Seletor_endereço ), .data(rom_1_data), .sel(1'b1));
  BitSelector #(.width(7), .group(5)) bitselector_1 (.in(rom_1_data), .out(out_2), .sel(1'b0));

  // Notes on the sheet:
  //   contents of rom_1 (hex, n*v repeats v):
  //   0 67 64 79 75 6e 71 6d 6f 65 72 70 76 6b 61 73 77 66 68 7a 69 6a 78 6c 74 62 63
endmodule

// R2
module Rotor2 (
  input  [4:0] \Seletor_endereço ,
  output [4:0] out_2
);

  wire [6:0] rom_1_data;

  BitSelector #(.width(7), .group(5)) bitselector_1 (.in(rom_1_data), .out(out_2), .sel(1'b0));
  ROM #(.addrWidth(5), .dataWidth(7)) rom_1 (.addr(\Seletor_endereço ), .data(rom_1_data), .sel(1'b1));

  // Notes on the sheet:
  //   contents of rom_1 (hex, n*v repeats v):
  //   0 67 64 79 75 6e 71 6d 6f 65 72 70 76 6b 61 73 77 66 68 7a 69 6a 78 6c 74 62 63
endmodule

// Controller!
module Controller__Inverso (
  input  [4:0] Letra,
  input  [4:0] Deslocamento,
  output [4:0] out_3
);

  wire comparator_1_eq, Sub;
  wire [4:0] multiplexer_1_out, subtractor_1_out, subtractor_2_out;

  Subtractor #(.width(5)) subtractor_1 (.a(Letra), .b(Deslocamento), .out(subtractor_1_out));  // open: bin, bout
  Comparator #(.width(5), .mode("unsigned")) comparator_1 (
    .a(subtractor_1_out), .b({5{1'b0}}), .eq(comparator_1_eq));  // open: gt, lt
  Comparator #(.width(5), .mode("unsigned")) comparator_2 (
    .a(subtractor_1_out), .b(5'b11010), .gt(Sub));  // open: eq, lt
  Multiplexer #(.width(5), .enable("false")) multiplexer_1 (
    .in0(subtractor_1_out), .in1(5'b11010), .out(multiplexer_1_out), .sel(comparator_1_eq));
  Subtractor #(.width(5)) subtractor_2 (.a(5'b11010), .b(Deslocamento), .out(subtractor_2_out));  // open: bin, bout
  Multiplexer #(.width(5), .enable("false")) multiplexer_2 (
    .in0(multiplexer_1_out), .in1(subtractor_2_out), .out(out_3), .sel(Sub));
endmodule

// R1!
module Rotor1__Inverso (
  input  [4:0] \Seletor_endereço ,
  output [4:0] out_2
);

  wire [6:0] rom_1_data;

  ROM #(.addrWidth(5), .dataWidth(7)) rom_1 (.addr(\Seletor_endereço ), .data(rom_1_data), .sel(1'b1));
  BitSelector #(.width(7), .group(5)) bitselector_1 (.in(rom_1_data), .out(out_2), .sel(1'b0));

  // Notes on the sheet:
  //   contents of rom_1 (hex, n*v repeats v):
  //   0 6e 79 7a 62 69 71 61 72 74 75 6d 77 67 65 68 6b 66 6a 6f 78 64 6c 70 76 63 73
endmodule

// R2!
module Rotor2__Inverso (
  input  [4:0] \Seletor_endereço ,
  output [4:0] out_2
);

  wire [6:0] rom_1_data;

  ROM #(.addrWidth(5), .dataWidth(7)) rom_1 (.addr(\Seletor_endereço ), .data(rom_1_data), .sel(1'b1));
  BitSelector #(.width(7), .group(5)) bitselector_1 (.in(rom_1_data), .out(out_2), .sel(1'b0));

  // Notes on the sheet:
  //   contents of rom_1 (hex, n*v repeats v):
  //   0 6e 79 7a 62 69 71 61 72 74 75 6d 77 67 65 68 6b 66 6a 6f 78 64 6c 70 76 63 73
endmodule
